// Digital circuit Contador.dig as structural Verilog
module Contador (
  input  In0,
  output Bit0,
  output Bit1
);

  ffjk ffjk_1 (.J(1'b1), .ck(In0), .K(1'b1), .Q(Bit1));  // open: Q_2
  ffjk ffjk_2 (.J(Bit1), .ck(In0), .K(Bit1), .Q(Bit0));  // open: Q_2
endmodule
