// Digital circuit Demux.dig as structural Verilog
module Demux (
  input  In0,
  input  In1,
  output O0,
  output O1,
  output O2,
  output O3
);

  wire not_1_out, not_2_out;

  not not_1 (not_1_out, In0);
  not not_2 (not_2_out, In1);
  and and_1 (O0, not_1_out, not_2_out);
  and and_2 (O1, not_1_out, In1);
  and and_3 (O2, In0, not_2_out);
  and and_4 (O3, In0, In1);
endmodule
