// Digital circuit PortaoTriState.dig as structural Verilog
module PortaoTriState (
  input  I0,
  input  I1,
  input  I2,
  input  I3,
  input  E,
  output O0,
  output O1,
  output O2,
  output O3
);

  assign O0 = E ? I0 : 1'bz;  // Driver driver_1
  assign O1 = E ? I1 : 1'bz;  // Driver driver_2
  assign O2 = E ? I2 : 1'bz;  // Driver driver_3
  assign O3 = E ? I3 : 1'bz;  // Driver driver_4
endmodule
