// Digital circuit arquivoPrincipalROM.dig as structural Verilog
module arquivoPrincipalROM (
  output O0,
  output O1,
  output O2,
  output O3
);

  wire contador_1_bit0, contador_1_bit1, contador_2_bit0, contador_2_bit1, contador_3_bit0, contador_3_bit1,
       contador_4_bit0, contador_4_bit1, contador_5_bit0, contador_5_bit1, demux_1_o0, demux_1_o1,
       demux_1_o2, demux_1_o3, demux_2_o0, demux_2_o1, demux_2_o2, demux_2_o3, demux_3_o0, demux_3_o1,
       demux_3_o2, demux_3_o3, demux_4_o0, demux_4_o1, demux_4_o2, demux_4_o3, demux_5_o0, demux_5_o1,
       demux_5_o2, demux_5_o3, Seletor_de_bloco_out, Seletor_de_Linha_out;

  Button Seletor_de_bloco (.out(Seletor_de_bloco_out));
  Contador contador_1 (.In0(Seletor_de_bloco_out), .Bit0(contador_1_bit0), .Bit1(contador_1_bit1));
  Demux demux_1 (
    .In0(contador_1_bit0), .In1(contador_1_bit1), .O0(demux_1_o0), .O1(demux_1_o1), .O2(demux_1_o2),
    .O3(demux_1_o3));
  Button Seletor_de_Linha (.out(Seletor_de_Linha_out));
  Contador contador_2 (.In0(Seletor_de_Linha_out), .Bit0(contador_2_bit0), .Bit1(contador_2_bit1));
  Contador contador_3 (.In0(Seletor_de_Linha_out), .Bit0(contador_3_bit0), .Bit1(contador_3_bit1));
  Contador contador_4 (.In0(Seletor_de_Linha_out), .Bit0(contador_4_bit0), .Bit1(contador_4_bit1));
  Contador contador_5 (.In0(Seletor_de_Linha_out), .Bit0(contador_5_bit0), .Bit1(contador_5_bit1));
  Demux demux_2 (
    .In0(contador_2_bit0), .In1(contador_2_bit1), .O0(demux_2_o0), .O1(demux_2_o1), .O2(demux_2_o2),
    .O3(demux_2_o3));
  Demux demux_3 (
    .In0(contador_3_bit0), .In1(contador_3_bit1), .O0(demux_3_o0), .O1(demux_3_o1), .O2(demux_3_o2),
    .O3(demux_3_o3));
  Demux demux_4 (
    .In0(contador_4_bit0), .In1(contador_4_bit1), .O0(demux_4_o0), .O1(demux_4_o1), .O2(demux_4_o2),
    .O3(demux_4_o3));
  Demux demux_5 (
    .In0(contador_5_bit0), .In1(contador_5_bit1), .O0(demux_5_o0), .O1(demux_5_o1), .O2(demux_5_o2),
    .O3(demux_5_o3));
  blocoROM Bloco_0 (
    .L0(demux_2_o0), .L1(demux_2_o1), .L2(demux_2_o2), .L3(demux_2_o3), .B00(1'b1), .B01(1'b0), .B02(1'b0),
    .B03(1'b0), .B10(1'b1), .B11(1'b0), .B12(1'b1), .B13(1'b0), .B20(1'b1), .B21(1'b0), .B22(1'b0),
    .B23(1'b1), .B30(1'b0), .B31(1'b0), .B32(1'b0), .B33(1'b0), .E(demux_1_o0), .O0(O0), .O1(O1), .O2(O2),
    .O3(O3));
  blocoROM Bloco_1 (
    .L0(demux_3_o0), .L1(demux_3_o1), .L2(demux_3_o2), .L3(demux_3_o3), .B00(1'b0), .B01(1'b0), .B02(1'b0),
    .B03(1'b1), .B10(1'b0), .B11(1'b1), .B12(1'b0), .B13(1'b1), .B20(1'b1), .B21(1'b0), .B22(1'b1),
    .B23(1'b1), .B30(1'b1), .B31(1'b1), .B32(1'b0), .B33(1'b1), .E(demux_1_o1), .O0(O0), .O1(O1), .O2(O2),
    .O3(O3));
  blocoROM Bloco_2 (
    .L0(demux_4_o0), .L1(demux_4_o1), .L2(demux_4_o2), .L3(demux_4_o3), .B00(1'b1), .B01(1'b1), .B02(1'b0),
    .B03(1'b0), .B10(1'b0), .B11(1'b1), .B12(1'b0), .B13(1'b0), .B20(1'b1), .B21(1'b1), .B22(1'b1),
    .B23(1'b1), .B30(1'b0), .B31(1'b0), .B32(1'b1), .B33(1'b0), .E(demux_1_o2), .O0(O0), .O1(O1), .O2(O2),
    .O3(O3));
  blocoROM Bloco_3 (
    .L0(demux_5_o0), .L1(demux_5_o1), .L2(demux_5_o2), .L3(demux_5_o3), .B00(1'b0), .B01(1'b0), .B02(1'b1),
    .B03(1'b1), .B10(1'b0), .B11(1'b1), .B12(1'b1), .B13(1'b0), .B20(1'b0), .B21(1'b1), .B22(1'b1),
    .B23(1'b1), .B30(1'b1), .B31(1'b1), .B32(1'b1), .B33(1'b0), .E(demux_1_o3), .O0(O0), .O1(O1), .O2(O2),
    .O3(O3));
endmodule
