// Digital circuit blocoROM.dig as structural Verilog
module blocoROM (
  input  L0,
  input  L1,
  input  L2,
  input  L3,
  input  B00,
  input  B01,
  input  B02,
  input  B03,
  input  B10,
  input  B11,
  input  B12,
  input  B13,
  input  B20,
  input  B21,
  input  B22,
  input  B23,
  input  B30,
  input  B31,
  input  B32,
  input  B33,
  input  E,
  output O0,
  output O1,
  output O2,
  output O3
);

  wire inst0_o0, inst0_o1, inst0_o2, inst0_o3;

  PortaoTriState inst0 (
    .I0(B00), .I1(B01), .I2(B02), .I3(B03), .E(L0), .O0(inst0_o0), .O1(inst0_o1), .O2(inst0_o2), .O3(inst0_o3));
  PortaoTriState inst1 (
    .I0(B10), .I1(B11), .I2(B12), .I3(B13), .E(L1), .O0(inst0_o0), .O1(inst0_o1), .O2(inst0_o2), .O3(inst0_o3));
  PortaoTriState inst2 (
    .I0(B20), .I1(B21), .I2(B22), .I3(B23), .E(L2), .O0(inst0_o0), .O1(inst0_o1), .O2(inst0_o2), .O3(inst0_o3));
  PortaoTriState inst3 (
    .I0(B30), .I1(B31), .I2(B32), .I3(B33), .E(L3), .O0(inst0_o0), .O1(inst0_o1), .O2(inst0_o2), .O3(inst0_o3));
  PortaoTriState seletor_bloco (
    .I0(inst0_o0), .I1(inst0_o1), .I2(inst0_o2), .I3(inst0_o3), .E(E), .O0(O0), .O1(O1), .O2(O2), .O3(O3));
endmodule
