// Digital circuit Contador.dig as structural Verilog
module Contador (
  input  In0,
  output Bit0,
  output Bit1
);

  JK_FF jk_ff_1 (.J(1'b1), .C(In0), .K(1'b1), .Q(Bit1));  // open: nQ
  JK_FF jk_ff_2 (.J(Bit1), .C(In0), .K(Bit1), .Q(Bit0));  // open: nQ
endmodule
