// Digital circuit PortaoTriState.dig as structural Verilog
module PortaoTriState (
  input  In0,
  input  In1,
  input  In2,
  input  In3,
  input  E,
  output O0,
  output O1,
  output O2,
  output O3
);

  assign O0 = E ? In0 : 1'bz;  // Driver driver_1
  assign O1 = E ? In1 : 1'bz;  // Driver driver_2
  assign O2 = E ? In2 : 1'bz;  // Driver driver_3
  assign O3 = E ? In3 : 1'bz;  // Driver driver_4
endmodule
