// Digital circuit arquivoPrincipalROM.dig as structural Verilog
module arquivoPrincipalROM (
  output O0,
  output O1,
  output O2,
  output O3
);

  wire Bloco_0_o0, Bloco_0_o1, Bloco_0_o2, Bloco_0_o3, Bloco_1_o0, Bloco_1_o1, Bloco_1_o2, Bloco_1_o3,
       Bloco_2_o0, Bloco_2_o1, Bloco_2_o2, Bloco_2_o3, Bloco_3_o0, Bloco_3_o1, Bloco_3_o2, Bloco_3_o3,
       contador_1_bit0, contador_1_bit1, contador_2_bit0, contador_2_bit1, contador_3_bit0, contador_3_bit1,
       contador_4_bit0, contador_4_bit1, contador_5_bit0, contador_5_bit1, seletor_1_p3, seletor_1_p4,
       seletor_1_p5, seletor_1_p6, seletor_2_p3, seletor_2_p4, seletor_2_p5, seletor_2_p6, seletor_3_p3,
       seletor_3_p4, seletor_3_p5, seletor_3_p6, seletor_4_p3, seletor_4_p4, seletor_4_p5, seletor_4_p6,
       seletor_5_p3, seletor_5_p4, seletor_5_p5, seletor_5_p6, Seletor_de_bloco_out, Seletor_de_Linha_out;

  Button Seletor_de_bloco (.out(Seletor_de_bloco_out));
  Contador contador_1 (.In0(Seletor_de_bloco_out), .Bit0(contador_1_bit0), .Bit1(contador_1_bit1));
  // Seletor seletor_1: pin names not known; wires that end beside it: contador_1_bit0, contador_1_bit1, seletor_1_p3, seletor_1_p4, seletor_1_p5, seletor_1_p6
  Button Seletor_de_Linha (.out(Seletor_de_Linha_out));
  Contador contador_2 (.In0(Seletor_de_Linha_out), .Bit0(contador_2_bit0), .Bit1(contador_2_bit1));
  Contador contador_3 (.In0(Seletor_de_Linha_out), .Bit0(contador_3_bit0), .Bit1(contador_3_bit1));
  Contador contador_4 (.In0(Seletor_de_Linha_out), .Bit0(contador_4_bit0), .Bit1(contador_4_bit1));
  Contador contador_5 (.In0(Seletor_de_Linha_out), .Bit0(contador_5_bit0), .Bit1(contador_5_bit1));
  // Seletor seletor_2: pin names not known; wires that end beside it: contador_2_bit0, contador_2_bit1, seletor_2_p3, seletor_2_p4, seletor_2_p5, seletor_2_p6
  // Seletor seletor_3: pin names not known; wires that end beside it: contador_3_bit0, contador_3_bit1, seletor_3_p3, seletor_3_p4, seletor_3_p5, seletor_3_p6
  // Seletor seletor_4: pin names not known; wires that end beside it: contador_4_bit0, contador_4_bit1, seletor_4_p3, seletor_4_p4, seletor_4_p5, seletor_4_p6
  // Seletor seletor_5: pin names not known; wires that end beside it: contador_5_bit0, contador_5_bit1, seletor_5_p3, seletor_5_p4, seletor_5_p5, seletor_5_p6
  blocoROM Bloco_0 (
    .L0(seletor_2_p3), .L1(seletor_2_p4), .L2(seletor_2_p5), .L3(seletor_2_p6), .B00(1'b1), .B01(1'b0),
    .B02(1'b0), .B03(1'b0), .B10(1'b1), .B11(1'b0), .B12(1'b1), .B13(1'b0), .B20(1'b1), .B21(1'b0),
    .B22(1'b0), .B23(1'b1), .B30(1'b0), .B31(1'b0), .B32(1'b0), .B33(1'b0), .O0(Bloco_0_o0), .O1(Bloco_0_o1),
    .O2(Bloco_0_o2), .O3(Bloco_0_o3));
  blocoROM Bloco_1 (
    .L0(seletor_3_p3), .L1(seletor_3_p4), .L2(seletor_3_p5), .L3(seletor_3_p6), .B00(1'b0), .B01(1'b0),
    .B02(1'b0), .B03(1'b1), .B10(1'b0), .B11(1'b1), .B12(1'b0), .B13(1'b1), .B20(1'b1), .B21(1'b0),
    .B22(1'b1), .B23(1'b1), .B30(1'b0), .B31(1'b0), .B32(1'b0), .B33(1'b1), .O0(Bloco_1_o0), .O1(Bloco_1_o1),
    .O2(Bloco_1_o2), .O3(Bloco_1_o3));
  blocoROM Bloco_2 (
    .L0(seletor_4_p3), .L1(seletor_4_p4), .L2(seletor_4_p5), .L3(seletor_4_p6), .B00(1'b1), .B01(1'b0),
    .B02(1'b0), .B03(1'b1), .B10(1'b0), .B11(1'b1), .B12(1'b0), .B13(1'b1), .B20(1'b1), .B21(1'b0),
    .B22(1'b0), .B23(1'b1), .B30(1'b0), .B31(1'b0), .B32(1'b0), .B33(1'b0), .O0(Bloco_2_o0), .O1(Bloco_2_o1),
    .O2(Bloco_2_o2), .O3(Bloco_2_o3));
  blocoROM Bloco_3 (
    .L0(seletor_5_p3), .L1(seletor_5_p4), .L2(seletor_5_p5), .L3(seletor_5_p6), .B00(1'b0), .B01(1'b0),
    .B02(1'b0), .B03(1'b1), .B10(1'b0), .B11(1'b1), .B12(1'b0), .B13(1'b1), .B20(1'b1), .B21(1'b0),
    .B22(1'b0), .B23(1'b1), .B30(1'b0), .B31(1'b0), .B32(1'b0), .B33(1'b0), .O0(Bloco_3_o0), .O1(Bloco_3_o1),
    .O2(Bloco_3_o2), .O3(Bloco_3_o3));
  PortaoTriState portaotristate_1 (
    .In0(Bloco_0_o0), .In1(Bloco_0_o1), .In2(Bloco_0_o2), .In3(Bloco_0_o3), .E(seletor_1_p3), .O0(O0),
    .O1(O1), .O2(O2), .O3(O3));
  PortaoTriState portaotristate_2 (
    .In0(Bloco_1_o0), .In1(Bloco_1_o1), .In2(Bloco_1_o2), .In3(Bloco_1_o3), .E(seletor_1_p4), .O0(O0),
    .O1(O1), .O2(O2), .O3(O3));
  PortaoTriState portaotristate_3 (
    .In0(Bloco_2_o0), .In1(Bloco_2_o1), .In2(Bloco_2_o2), .In3(Bloco_2_o3), .E(seletor_1_p5), .O0(O0),
    .O1(O1), .O2(O2), .O3(O3));
  PortaoTriState portaotristate_4 (
    .In0(Bloco_3_o0), .In1(Bloco_3_o1), .In2(Bloco_3_o2), .In3(Bloco_3_o3), .E(seletor_1_p6), .O0(O0),
    .O1(O1), .O2(O2), .O3(O3));
endmodule
