// Digital circuit bloco4bits.dig as structural Verilog
module bloco4bits (
  input  in_1,
  input  in_2,
  input  in_3,
  input  in_4,
  input  in_5,
  output out_6,
  output out_7,
  output out_8,
  output out_9
);

  assign out_6 = in_5 ? in_1 : 1'bz;  // Driver driver_1
  assign out_7 = in_5 ? in_2 : 1'bz;  // Driver driver_2
  assign out_8 = in_5 ? in_3 : 1'bz;  // Driver driver_3
  assign out_9 = in_5 ? in_4 : 1'bz;  // Driver driver_4
endmodule
