// Digital circuit blocoROM.dig as structural Verilog
module blocoROM (
  input  L0,
  input  L1,
  input  L2,
  input  L3,
  input  B00,
  input  B01,
  input  B02,
  input  B03,
  input  B10,
  input  B11,
  input  B12,
  input  B13,
  input  B20,
  input  B21,
  input  B22,
  input  B23,
  input  B30,
  input  B31,
  input  B32,
  input  B33,
  output O0,
  output O1,
  output O2,
  output O3
);

  bloco4bits inst0 (.In0(B00), .In1(B01), .In2(B02), .In3(B03), .L(L0), .Out0(O0), .Out1(O1), .Out2(O2), .Out3(O3));
  bloco4bits inst1 (.In0(B10), .In1(B11), .In2(B12), .In3(B13), .L(L1), .Out0(O0), .Out1(O1), .Out2(O2), .Out3(O3));
  bloco4bits inst2 (.In0(B20), .In1(B21), .In2(B22), .In3(B23), .L(L2), .Out0(O0), .Out1(O1), .Out2(O2), .Out3(O3));
  bloco4bits inst3 (.In0(B30), .In1(B31), .In2(B32), .In3(B33), .L(L3), .Out0(O0), .Out1(O1), .Out2(O2), .Out3(O3));
endmodule
