// Digital circuit ffjk.dig as structural Verilog
module ffjk (
  input  J,
  input  ck,
  input  K,
  output Q,
  output Q_2
);

  wire nand_1_out, nand_2_out, nand_3_out, nand_4_out, nand_5_out, nand_6_out, not_1_out;

  nand nand_1 (nand_1_out, Q_2, J, ck);
  nand nand_2 (nand_2_out, ck, K, Q);
  nand nand_3 (nand_3_out, nand_1_out, nand_4_out);
  not not_1 (not_1_out, ck);
  nand nand_4 (nand_4_out, nand_3_out, nand_2_out);
  nand nand_5 (nand_5_out, nand_3_out, not_1_out);
  nand nand_6 (nand_6_out, not_1_out, nand_4_out);
  nand nand_7 (Q, nand_5_out, Q_2);
  nand nand_8 (Q_2, Q, nand_6_out);
endmodule
