// Digital circuit 4BitAdder.dig as structural Verilog
module _4BitAdder (
  input  Ci,
  input  X3,
  input  X2,
  input  X1,
  input  X0,
  input  Y3,
  input  Y2,
  input  Y1,
  input  Y0,
  input  Co1,
  input  Co2,
  output O3,
  output O2,
  output O1,
  output O0,
  output Co,
  output OF,
  output Zr,
  output Ng
);

  wire adder_1_ti_plus_1, adder_2_ti_plus_1, adder_3_ti_plus_1, and_2_out, and_3_out, not_1_out, not_2_out,
       not_3_out, or_1_out;

  Adder adder_1 (.Ai(X3), .Bi(Y3), .Ti(Ci), .Oi(O3), .Ti_plus_1(adder_1_ti_plus_1));
  Adder adder_2 (.Ai(X2), .Bi(Y2), .Ti(adder_1_ti_plus_1), .Oi(O2), .Ti_plus_1(adder_2_ti_plus_1));
  Adder adder_3 (.Ai(X1), .Bi(Y1), .Ti(adder_2_ti_plus_1), .Oi(O1), .Ti_plus_1(adder_3_ti_plus_1));
  Adder adder_4 (.Ai(X0), .Bi(Y0), .Ti(adder_3_ti_plus_1), .Oi(O0), .Ti_plus_1(Co));
  or or_1 (or_1_out, Co1, Co2);
  not not_1 (not_1_out, Y0);
  not not_2 (not_2_out, X0);
  and and_1 (Ng, O0, or_1_out);
  not not_3 (not_3_out, O0);
  and and_2 (and_2_out, not_3_out, X0, Y0);
  and and_3 (and_3_out, O0, not_2_out, not_1_out);
  nor nor_1 (Zr, O3, O2, O1, O0);
  or or_2 (OF, and_2_out, and_3_out);
endmodule
