// Digital circuit Adder.dig as structural Verilog
module Adder (
  input  Ai,
  input  Bi,
  input  Ti,
  output Oi,
  output Ti_plus_1
);

  wire and_1_out, and_2_out, and_3_out, xor_1_out;

  xor xor_1 (xor_1_out, Bi, Ti);
  and and_1 (and_1_out, Ai, Bi);
  and and_2 (and_2_out, Ai, Ti);
  and and_3 (and_3_out, Bi, Ti);
  xor xor_2 (Oi, Ai, xor_1_out);
  or or_1 (Ti_plus_1, and_1_out, and_2_out, and_3_out);
endmodule
