// Digital circuit BlocoComplemento.dig as structural Verilog
module BlocoComplemento (
  input  I0,
  input  I1,
  input  I2,
  input  I3,
  input  E,
  output O0,
  output O1,
  output O2,
  output O3
);

  wire _4bitadder_1_co, _4bitadder_1_ng, _4bitadder_1_o0, _4bitadder_1_o1, _4bitadder_1_o2, _4bitadder_1_o3,
       _4bitadder_1_of, _4bitadder_1_zr, not_1_out, not_2_out, not_3_out, not_4_out, not_5_out;

  not not_1 (not_1_out, E);
  not not_2 (not_2_out, I0);
  not not_3 (not_3_out, I1);
  not not_4 (not_4_out, I2);
  not not_5 (not_5_out, I3);
  _4BitAdder _4bitadder_1 (
    .Ci(1'b0), .X3(not_5_out), .X2(not_4_out), .X1(not_3_out), .X0(not_2_out), .Y3(1'b1), .Y2(1'b0),
    .Y1(1'b0), .Y0(1'b0), .Co1(1'b0), .Co2(1'b0), .O3(_4bitadder_1_o3), .O2(_4bitadder_1_o2),
    .O1(_4bitadder_1_o1), .O0(_4bitadder_1_o0), .Co(_4bitadder_1_co), .OF(_4bitadder_1_of),
    .Zr(_4bitadder_1_zr), .Ng(_4bitadder_1_ng));
  assign O0 = E ? _4bitadder_1_o0 : 1'bz;  // Driver driver_1
  assign O0 = not_1_out ? I0 : 1'bz;  // Driver driver_2
  assign O1 = E ? _4bitadder_1_o1 : 1'bz;  // Driver driver_3
  assign O1 = not_1_out ? I1 : 1'bz;  // Driver driver_4
  assign O2 = E ? _4bitadder_1_o2 : 1'bz;  // Driver driver_5
  assign O2 = not_1_out ? I2 : 1'bz;  // Driver driver_6
  assign O3 = E ? _4bitadder_1_o3 : 1'bz;  // Driver driver_7
  assign O3 = not_1_out ? I3 : 1'bz;  // Driver driver_8
endmodule
