// Digital circuit Geral.dig as structural Verilog
module Geral (
  input  X3,
  input  X2,
  input  X1,
  input  X0,
  input  Y3,
  input  Y2,
  input  Y1,
  input  Y0,
  input  F0,
  input  F1,
  input  F2,
  input  F3,
  output Bit_3,
  output Bit_2,
  output Bit_1,
  output Bit_0,
  output Carry,
  output Overflow,
  output Zero,
  output Negativo
);

  wire blococomplemento_1_o0, blococomplemento_1_o1, blococomplemento_1_o2, blococomplemento_1_o3,
       blococomplemento_2_o0, blococomplemento_2_o1, blococomplemento_2_o2, blococomplemento_2_o3,
       decoder_1_o0, decoder_1_o1, decoder_1_o2, decoder_1_o3, zerador_1_o0, zerador_1_o1, zerador_1_o2,
       zerador_1_o3;

  Decoder decoder_1 (
    .I0(F0), .I1(F1), .I2(F2), .I3(F3), .O0(decoder_1_o0), .O1(decoder_1_o1), .O2(decoder_1_o2),
    .O3(decoder_1_o3));
  BlocoComplemento blococomplemento_1 (
    .I0(X0), .I1(X1), .I2(X2), .I3(X3), .E(decoder_1_o0), .O0(blococomplemento_1_o0),
    .O1(blococomplemento_1_o1), .O2(blococomplemento_1_o2), .O3(blococomplemento_1_o3));
  BlocoComplemento blococomplemento_2 (
    .I0(Y0), .I1(Y1), .I2(Y2), .I3(Y3), .E(decoder_1_o1), .O0(blococomplemento_2_o0),
    .O1(blococomplemento_2_o1), .O2(blococomplemento_2_o2), .O3(blococomplemento_2_o3));
  Zerador zerador_1 (
    .I0(blococomplemento_2_o0), .I1(blococomplemento_2_o1), .I2(blococomplemento_2_o2),
    .I3(blococomplemento_2_o3), .E(decoder_1_o2), .O0(zerador_1_o0), .O1(zerador_1_o1), .O2(zerador_1_o2),
    .O3(zerador_1_o3));
  _4BitAdder _4bitadder_1 (
    .Ci(decoder_1_o3), .X3(blococomplemento_1_o3), .X2(blococomplemento_1_o2), .X1(blococomplemento_1_o1),
    .X0(blococomplemento_1_o0), .Y3(zerador_1_o3), .Y2(zerador_1_o2), .Y1(zerador_1_o1), .Y0(zerador_1_o0),
    .Co1(decoder_1_o0), .Co2(decoder_1_o1), .O3(Bit_3), .O2(Bit_2), .O1(Bit_1), .O0(Bit_0), .Co(Carry),
    .OF(Overflow), .Zr(Zero), .Ng(Negativo));
endmodule
