// Digital circuit Zerador.dig as structural Verilog
module Zerador (
  input  I0,
  input  I1,
  input  I2,
  input  I3,
  input  E,
  output O0,
  output O1,
  output O2,
  output O3
);

  wire not_1_out;

  not not_1 (not_1_out, E);
  assign O0 = not_1_out ? I0 : 1'bz;  // Driver driver_1
  assign O1 = not_1_out ? I1 : 1'bz;  // Driver driver_2
  assign O2 = not_1_out ? I2 : 1'bz;  // Driver driver_3
  assign O3 = not_1_out ? I3 : 1'bz;  // Driver driver_4
  assign O0 = E ? 1'b0 : 1'bz;  // Driver driver_5
  assign O1 = E ? 1'b0 : 1'bz;  // Driver driver_6
  assign O2 = E ? 1'b0 : 1'bz;  // Driver driver_7
  assign O3 = E ? 1'b0 : 1'bz;  // Driver driver_8
endmodule
